# Fritzing sketch Pinchy (saved by Fritzing 0.9.3b)

parts:
  J11 = female pin header, 15 pins [form="♀ (female)"]
  J12 = female pin header, 15 pins [form="♀ (female)"]
  U1 = DC-DC 2-24V Step Up Booster [part_number="XL6009 2a Boost Converter DC 6v" package=THT]
  BAT1 = Battery Holders [package=battery-aa-kit]
  BAT2 = Battery Holders [package=battery-aa-kit]
  BAT3 = Battery Holders [package=battery-aa-kit]
  ULN2003_(Left) = ULN2003A breakout board
  MOT3 = 28BYJ-48 Stepper Motor [part_number=24BYJ48]
  ULN2003_(Right) = ULN2003A breakout board
  MOT4 = 28BYJ-48 Stepper Motor [part_number=24BYJ48]
  MOT1 = Basic Servo [part_number="MG90S (Elevator Servo)"]
  MOT2 = Basic Servo [part_number="MG90S (Gripper Servo)"]
  J9 = male pin header, 3 pins [form="♂ (male)"]
  J10 = male pin header, 3 pins [form="♂ (male)"]
  J1 = Screw terminal - 2 pins [package=THT]
  S1 = Toggle Switch [package=THT]
  LED1 = LED - 3mm [color="White (4500K)" package="3 mm [THT]"]
  LED2 = LED - 3mm [color="White (4500K)" package="3 mm [THT]"]
  J2 = female pin header, 2 pins [form="♀ (female)"]
  Q1 = npn-Powertransistor [part_number=FQP30N06L package="TO220 [THT]"]
  S2 = TILT-SWITCH-SW-200D [part_number=SW-200D package=reed_switch_plastic]
  R4 = Resistor [tolerance=±5% resistance=1k package=THT]
  R2 = Resistor [tolerance=±5% resistance=220 package=THT]
  R1 = Resistor [tolerance=±5% resistance=220 package=THT]
  Q2 = NPN-Transistor [part_number=BC548 package="TO92 [THT]"]
  R7 = Resistor [tolerance=±5% resistance=10k package=THT]
  R3 = Resistor [tolerance=±5% resistance=220 package=THT]
  R8 = Resistor [tolerance=±5% resistance=10k package=THT]
  R6 = Resistor [tolerance=±5% resistance=1k package=THT]
  R5 = Resistor [tolerance=±5% resistance=1k package=THT]
  J8 = male pin header, 2 pins [form="♂ (male)"]
  J7 = male pin header, 2 pins [form="♂ (male)"]
  J13 = male pin header, 4 pins [form="♂ (male)"]
  J14 = male pin header, 4 pins [form="♂ (male)"]
  J5 = female pin header, 1 pin [form="♀ (female)"]
  J6 = female pin header, 1 pin [form="♀ (female)"]
  J3 = female pin header, 1 pin [form="♀ (female)"]
  J4 = female pin header, 1 pin [form="♀ (female)"]
  M1 = DOIT Esp32 DevKit v1 (30 pins long, 11 pins width) [part_number=ESP32S-PIN30]
  J15 = male pin header, 2 pins [form="♂ (male)"]
  J16 = male pin header, 2 pins [form="♂ (male)"]

nets:
  N1: J11.pin8, S2.1, M1.D25
  N2: J11.pin9, LED2.anode, J7.pin2, M1.D26
  N3: J11.pin10, LED1.anode, J8.pin2, M1.D27
  N4: J11.pin11, MOT1.pulse, J9.pin3, R5.Pin_0, M1.D14
  N5: J11.pin12, MOT2.pulse, J10.pin3, R6.Pin_0, M1.D12
  N6: J11.pin13, R7.Pin_0, R3.Pin_0, M1.D13
  GND: J11.pin14, J12.pin2, U1.pin2, U1.pin4, BAT1.-, ULN2003_(Left).0V, ULN2003_(Right).0V, J1.pin1, Q1.emitter, R4.Pin_1, R2.Pin_1, R1.Pin_1, Q2.E, R7.Pin_1, R6.Pin_1, R5.Pin_1, J5.pin1, J3.pin1, M1.GND, J15.pin1, J16.pin1
  6V: J11.pin15, U1.pin1, ULN2003_(Left).+5V, ULN2003_(Right).+5V, MOT1.vcc, MOT2.vcc, J9.pin2, J10.pin2, R8.Pin_0, J6.pin1, M1.VIN, J15.pin2, J16.pin2
  N7: J12.pin3, ULN2003_(Left).In_4, J14.pin4, M1.D15
  N8: J12.pin4, ULN2003_(Left).In_3, J14.pin3, M1.D2
  N9: J12.pin5, ULN2003_(Left).In_2, J14.pin2, M1.D4
  N10: J12.pin9, ULN2003_(Left).In_1, J14.pin1, M1.D18
  N11: J12.pin10, ULN2003_(Right).In_4, J13.pin4, M1.D19
  N12: J12.pin11, ULN2003_(Right).In_3, J13.pin3, M1.D21
  N13: J12.pin14, ULN2003_(Right).In_2, J13.pin2, M1.D22
  N14: J12.pin15, ULN2003_(Right).In_1, J13.pin1, M1.D23
  N15: U1.pin3, S1.L1, J2.pin2, J4.pin1
  N16: BAT1.+, BAT2.-
  N17: BAT2.+, BAT3.-
  N18: BAT3.+, J1.pin2, S1.COM, J2.pin1
  N19: ULN2003_(Left).RED_wire, MOT3.RED
  N20: ULN2003_(Left).ORANGE_wire, MOT3.ORANGE
  N21: ULN2003_(Left).YELLOW_wire, MOT3.YELLOW
  N22: ULN2003_(Left).PINK_wire, MOT3.PINK
  N23: ULN2003_(Left).BLUE_wire, MOT3.BLUE
  N24: ULN2003_(Right).RED_wire, MOT4.RED
  N25: ULN2003_(Right).ORANGE_wire, MOT4.ORANGE
  N26: ULN2003_(Right).YELLOW_wire, MOT4.YELLOW
  N27: ULN2003_(Right).PINK_wire, MOT4.PINK
  N28: ULN2003_(Right).BLUE_wire, MOT4.BLUE
  GND_2: MOT1.gnd, MOT2.gnd, J9.pin1, J10.pin1, Q1.collector
  N29: LED1.cathode, R1.Pin_0, J8.pin1
  N30: LED2.cathode, R2.Pin_0, J7.pin1
  N31: Q1.base, Q2.C, R8.Pin_1
  N32: S2.2, R4.Pin_0
  N33: Q2.B, R3.Pin_1

notes:
  +4.5v
  +6v
  Elevator Servo
  Gripper Servo
  Left Wheel Stepper Motor (28BYJ-48)
  Right Wheel Stepper Motor (28BYJ-48)
  3x AA Batteries
  Servo Power Control
  Motion Sensor
  Right Headlight
  ESP32 Dev Board (30 pin)
  Right Wheel Stepper Driver (ULN2003)
  Left Wheel Stepper Driver (ULN2003)
  Power Switch
  Boost Converter
  Left Headlight

custom parts:
  DC-DC 2-24V Step Up Booster: Convertisseur DC-DC 2-24V 2A
  ULN2003A breakout board: ULN2003A 7-way Darlington Transistor Driver on breakoutboard
  DOIT Esp32 DevKit v1 (30 pins long, 11 pins width): The DOIT Esp32 DevKit v1 is one of the development board created by DOIT to evaluate the ESP-WROOM-32 module. It is based on the ESP32 microcontroller that boasts Wifi, Bluetooth, Ethernet and Low Power support all in a single chip. (vanepp) made breadboard work, adjusted pin numbering and labels and reduced size of schematic and cleaned up pcb. This chip is 30pins long (2 x15) and 11 pins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
